# Fritzing sketch SimpleSwitch (saved by Fritzing 0.9.3b)
circuit board: 1.18533cm x 1.82504cm
breadboards: 1

parts:
  Raspberry_Pi1 = Raspberry Pi 2
  LED1 = LED - 5mm [color="Red (633nm)" package="5 mm [THT]"]
  R1 = Resistor [tolerance=±5% resistance=100 package="0402 [SMD]"]

nets (from the breadboard view):
  N1: Raspberry_Pi1.GPIO7, R1.Pin_0
  N2: Raspberry_Pi1.GND, LED1.cathode
  N3: LED1.anode, R1.Pin_1
