# Fritzing sketch l3gd20-bme280 (saved by Fritzing 0.9.3b)
breadboards: 1

parts:
  Raspberry_Pi_1 = Raspberry Pi 3 [part_number=RPI-3-V1.2]
  Part1 = L3GD20H Triple-Axis Gyro Breakout Board [part_number=1032]
  Part2 = Adafruit BME280

nets:
  N1: Raspberry_Pi_1.GPIO2, Part1.SDA/SDI/SDO, Part2.SDI/SDA
  N2: Raspberry_Pi_1.GPIO3, Part1.SCL/SPC, Part2.SCK/SCL
  3V3: Raspberry_Pi_1.3V3, Part1.+3V3, Part2.3.3V
  GND: Raspberry_Pi_1.GND, Part1.GND, Part2.GND

custom parts:
  L3GD20H Triple-Axis Gyro Breakout Board: This breakout board is based around the latest gyro technology, the L3GD20H from STMicro. It's the upgrade to the L3G4200 with three full axes of sensing. The chip can be set to ±250, ±500, or ±2000 degree-per-second scale for a large range of sensitivity. The chip supports both I2C and SPI so you can interface with any microcontroller easily. Includes level shifting circuitry so you can use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
  Adafruit BME280: Bosch has stepped up their game with their new BME280 sensor, an environmental sensor with temperature, barometric pressure and humidity! This sensor is great for all sorts of weather/environmental sensing and can even be used in both I2C and SPI! This precision sensor from Bosch is the best low-cost sensing solution for measuring humidity with ±3% accuracy, barometric pressure with ±1 hPa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
