# Fritzing sketch mcp3008 (saved by Fritzing 0.9.3b)
breadboards: 1

parts:
  IC1 = MCP3008 8-channel 10-bit ADC [part_number=MCP3008]
  U1 = POT [package=pot_mammoth]
  Raspberry_Pi_1 = Raspberry Pi 3 [part_number=RPI-3-V1.2]

nets:
  N1: IC1.no_name_yet#1, U1.A
  N2: IC1.no_name_yet#9, IC1.no_name_yet#14, U1.S, Raspberry_Pi_1.GND
  N3: IC1.no_name_yet#10, Raspberry_Pi_1.GIPO25
  N4: IC1.no_name_yet#11, Raspberry_Pi_1.GIPO24
  N5: IC1.no_name_yet#12, Raspberry_Pi_1.GIPO23
  N6: IC1.no_name_yet#13, Raspberry_Pi_1.GIPO18
  N7: IC1.no_name_yet#15, IC1.no_name_yet#16, U1.E, Raspberry_Pi_1.3v3
